# Fritzing sketch rPiezos_sketch (saved by Fritzing 0.9.3b)
breadboards: 1

parts:
  IC1 = IC, DIP package, 16 pins [chip_label=MCP3008]
  Raspberry_Pi_1 = Raspberry Pi 3 [part_number=RPI-3-V1.2]
  D1 = Rectifier Diode
  R1 = Resistor [tolerance=±5% resistance=1M package=THT]
  TRS1 = Audio Jack (TRS) 3.5mm [package="PG203J [THT]"]
  R3 = Resistor [tolerance=±5% resistance=1.8k package=THT]
  R2 = Resistor [tolerance=±5% resistance=560 package=THT]

nets:
  N1: IC1.pin1, R3.Pin_1, R2.Pin_1
  N2: IC1.pin9, IC1.pin14, Raspberry_Pi_1.GND, D1.cathode, R1.Pin_0, TRS1.Tip, R3.Pin_0
  N3: IC1.pin10, Raspberry_Pi_1.GIPO8
  N4: IC1.pin11, Raspberry_Pi_1.GIPO10
  N5: IC1.pin12, Raspberry_Pi_1.GIPO9
  N6: IC1.pin13, Raspberry_Pi_1.GIPO11
  N7: IC1.pin15, IC1.pin16, Raspberry_Pi_1.5V
  N8: D1.anode, R1.Pin_1, TRS1.Ring, R2.Pin_0

custom parts:
  Rectifier Diode: Ageneral purpose zener diode
